# Fritzing sketch DataCollector.Device_Schematic (saved by Fritzing 0.9.3b)
circuit board: 11.6925cm x 8.02485cm
breadboards: 1

parts:
  Raspberry_Pi_2 = Raspberry Pi 3 [part_number=RPI-3-V1.2]
  R2 = Resistor [tolerance=±5% resistance=220 package=THT]
  LED1 = LEDs [package=led10mm]
  U1 = PCF8574 [package="DIP16 [THT]"]
  Q1 = NPN-Transistor [package="TO92 [THT]"]
  Part1 = Barometric Pressure Sensor - BMP085 Breakout
  U2 = SHT1x Humdity Sensor [package=sht1x]
  R3 = Resistor [tolerance=±5% resistance=220 package=THT]
  GY2 = MPU-6050 Board GY-521 [form="♀ (female)" package=THT]

nets:
  VCC: Raspberry_Pi_2.3v3, U1.VCC, Q1.C, Part1.VCC, U2.VDD, GY2.pin1
  N1: Raspberry_Pi_2.GPIO2, U1.SDA, Part1.SDA, U2.SDA, GY2.pin4
  N2: Raspberry_Pi_2.GPIO3, U1.SCL, Part1.SCL, U2.SCL, GY2.pin3
  GND: Raspberry_Pi_2.GND, LED1.C, U1.GND, Part1.GND, U2.GND, GY2.pin2
  N3: R2.Pin_0, Q1.E
  N4: R2.Pin_1, LED1.A
  N5: U1.P3, R3.Pin_0
  N6: Q1.B, R3.Pin_1

custom parts:
  SHT1x Humdity Sensor: SHT1x Humdity Sensor Sensirion humdity sensor. Schematic element and footprint proven. Spark Fun Electronics SKU : COM-08227
  MPU-6050 Board GY-521: Acelerometro y Giroscopio MPU-6050 Board GY-521
